// Logisim project CarryLookAheadAdder.circ as structural Verilog: 1 circuit, main circuit main
module main (
  input  C0,
  input  [3:0] A,
  input  [3:0] B,
  input  in_4
);

  wire and_1_out, and_2_out, and_3_out, and_4_out, and_5_out, and_6_out, and_7_out, and_8_out, and_9_out,
       and_10_out, C1_out, C2_out, C3_out, G0_out, G1_out, G2_out, G3_out, P0_out, P1_out, P2_out, P3_out;
  wire [0:0] C4_out;
  wire [3:0] S0_out;

  xor P0 (P0_out, A[0], B[0]);
  and G0 (G0_out, A[0], B[0]);
  xor P1 (P1_out, A[1], B[1]);
  and G1 (G1_out, A[1], B[1]);
  xor P2 (P2_out, A[2], B[2]);
  and G2 (G2_out, A[2], B[2]);
  xor P3 (P3_out, A[3], B[3]);
  and G3 (G3_out, A[3], B[3]);
  and and_1 (and_1_out, C0, P0_out);
  and and_2 (and_2_out, P0_out, P1_out, C0);
  and and_3 (and_3_out, P1_out, G0_out);
  and and_4 (and_4_out, C0, P0_out, P1_out, P2_out);
  and and_5 (and_5_out, P1_out, P2_out, G0_out);
  and and_6 (and_6_out, P2_out, G1_out);
  and and_7 (and_7_out, C0, P0_out, P1_out, P2_out, P3_out);
  and and_8 (and_8_out, G0_out, P1_out, P2_out, P3_out);
  and and_9 (and_9_out, G1_out, P2_out, P3_out);
  and and_10 (and_10_out, G2_out, P3_out);
  or C1 (C1_out, and_1_out, G0_out);
  or C2 (C2_out, G1_out, and_2_out, and_3_out);
  or C3 (C3_out, G2_out, and_4_out, and_5_out, and_6_out);
  or C4 (C4_out[0], and_7_out, and_8_out, and_9_out, and_10_out, G3_out);
  xor S0 (S0_out[0], C0, P0_out);
  xor S1 (S0_out[1], C1_out, P1_out);
  xor S2 (S0_out[2], C2_out, P2_out);
  xor S3 (S0_out[3], C3_out, P3_out);
  Hex_Digit_Display hex_digit_display_1 (.value({{3{in_4}}, C4_out[0]}));  // open: dp
  Hex_Digit_Display hex_digit_display_2 (.value(S0_out));  // open: dp
endmodule
