// Logisim project universal_shift_register_circuit.circ as structural Verilog: 1 circuit, main circuit main
module main (
  input  set,
  input  left,
  input  preset,
  input  right,
  input  [1:0] s,
  input  d1,
  input  d2,
  input  d3,
  input  d4,
  output q3,
  output q2,
  output q1,
  output q0
);

  wire clock_1_out, multiplexer_1_out, multiplexer_2_out, multiplexer_3_out, multiplexer_4_out;

  Multiplexer #(.select(2)) multiplexer_1 (.in0(d1), .in1(q2), .in2(right), .in3(q3), .out(multiplexer_1_out), .sel(s));
  Multiplexer #(.select(2)) multiplexer_2 (.in0(d2), .in1(q1), .in2(q3), .in3(q2), .out(multiplexer_2_out), .sel(s));
  Multiplexer #(.select(2)) multiplexer_3 (.in0(d3), .in1(q0), .in2(q2), .in3(q1), .out(multiplexer_3_out), .sel(s));
  Multiplexer #(.select(2)) multiplexer_4 (.in0(d4), .in1(left), .in2(q1), .in3(q0), .out(multiplexer_4_out), .sel(s));
  Clock clock_1 (.out(clock_1_out));
  D_Flip_Flop d_ff_1 (.D(multiplexer_1_out), .clk(clock_1_out), .Q(q3), .preset(set), .reset(preset));  // open: Qn
  D_Flip_Flop d_ff_2 (.D(multiplexer_2_out), .clk(clock_1_out), .Q(q2), .preset(set), .reset(preset));  // open: Qn
  D_Flip_Flop d_ff_3 (.D(multiplexer_3_out), .clk(clock_1_out), .Q(q1), .preset(set), .reset(preset));  // open: Qn
  D_Flip_Flop d_ff_4 (.D(multiplexer_4_out), .clk(clock_1_out), .Q(q0), .preset(set), .reset(preset));  // open: Qn

  // Notes on the sheet:
  //   0 for parallel
  //   1 for left
  //   2 for right
  //    3 for retain
endmodule
